# Fritzing sketch RPi Reed Switch (saved by Fritzing 0.9.2b)
breadboards: 1

parts:
  Raspberry_Pi1 = Raspberry Pi 2
  R1 = Resistor [tolerance=±5% resistance=220 package=THT]
  S1 = Reed switch [package=THT]

nets:
  N1: Raspberry_Pi1.3v3, S1.pin_2
  N2: Raspberry_Pi1.GND, R1.Pin_1
  N3: Raspberry_Pi1.GPIO17, R1.Pin_0, S1.pin_1
